# Fritzing sketch sketch (saved by Fritzing 0.9.3b)

parts:
  U1 = NodeMCU V1.0
  DHT1 = DHT22 Humidity and Temperature Sensor
  Part1 = Soil Moisture Sensor
  VCC1 = Battery

nets:
  N1: U1.D2, DHT1.DATA
  GND: U1.GND, DHT1.GND, Part1.GND, VCC1.-
  3V3: U1.3V3, DHT1.VDD, Part1.VCC
  N2: U1.Vin, VCC1.+
  N3: U1.A0, Part1.SIG

custom parts:
  NodeMCU V1.0: ESP8266 based NodeMCU
